# Fritzing sketch DA3B (saved by Fritzing 0.9.3b)

parts:
  MFS1 = Multi Function Shield
  Part2 = FTDI Basic Programmer
  T1 = LM34 Temperature Sensor [package="TO92 [THT]"]

nets:
  GND: MFS1.GND, Part2.GND, T1.GND
  N1: MFS1.RESET, Part2.DTR
  N2: MFS1.5V, MFS1.VCC#100, Part2.POWER
  N3: MFS1.1, Part2.RXI
  N4: MFS1.0, Part2.TXO
  N5: MFS1.J1-A4, T1.Vout
  N6: MFS1.VCC#106, T1.+Vs

notes:
  USB to PC

custom parts:
  Multi Function Shield: Das Multi Function Shield kann auf den Arduino Uno aufgesteckt werden und bietet ein paar wichtige Bauteile.
