# Fritzing sketch DA4A (saved by Fritzing 0.9.3b)
breadboards: 1

parts:
  MFS1 = Multi Function Shield
  Part1 = Motor Driver 1A Dual TB6612FNG  # not connected
  R1 = TRIMPOT [package=3362u-2]
  M1 = DC Motor  # not connected

nets:
  N1: MFS1.A0, R1.WIPER
  5V: MFS1.5V, MFS1.VCC, R1.CW
  N2: MFS1.GND, R1.CCW

custom parts:
  Multi Function Shield: Das Multi Function Shield kann auf den Arduino Uno aufgesteckt werden und bietet ein paar wichtige Bauteile.
