# Fritzing sketch servo (saved by Fritzing 0.9.3b)

parts:
  MFS1 = Multi Function Shield
  J1 = Basic Servo

nets:
  N1: MFS1.D9_PWM, J1.pulse
  VCC: MFS1.5V, MFS1.VCC, J1.vcc
  GND: MFS1.GND, J1.gnd

custom parts:
  Multi Function Shield: Das Multi Function Shield kann auf den Arduino Uno aufgesteckt werden und bietet ein paar wichtige Bauteile.
