# Fritzing sketch stepper (saved by Fritzing 0.9.3b)

parts:
  MFS1 = Multi Function Shield
  BREAKOUT1 = ULN2003A breakout board
  M1 = Stepper Motor - Unipolar

nets:
  N1: MFS1.D8, BREAKOUT1.In_4
  N2: MFS1.D9_PWM, BREAKOUT1.In_3
  N3: MFS1.D10_PWM/SS, BREAKOUT1.In_2
  N4: MFS1.D11_PWM/MOSI, BREAKOUT1.In_1
  5V: MFS1.5V, MFS1.VCC, BREAKOUT1.+5V
  N5: MFS1.GND, BREAKOUT1.0V
  N6: BREAKOUT1.RED_wire, M1.COMMON_2
  N7: BREAKOUT1.ORANGE_wire, M1.B
  N8: BREAKOUT1.YELLOW_wire, M1.C
  N9: BREAKOUT1.PINK_wire, M1.COMMON_1
  N10: BREAKOUT1.BLUE_wire, M1.A

custom parts:
  Multi Function Shield: Das Multi Function Shield kann auf den Arduino Uno aufgesteckt werden und bietet ein paar wichtige Bauteile.
  ULN2003A breakout board: ULN2003A 7-way Darlington Transistor Driver on breakoutboard
