# Fritzing sketch DA6 (saved by Fritzing 0.9.3b)

parts:
  Part1 = InvenSense MPU6050
  Part2 = FTDI Basic Programmer
  MFS1 = Multi Function Shield

nets:
  VCC: Part1.VCC, MFS1.5V, MFS1.VCC
  N1: Part1.GND, MFS1.GND#88, MFS1.GND#92
  N2: Part1.SCL, MFS1.A5/SCL
  N3: Part1.SDA, MFS1.A4/SDA
  N4: Part2.RXI, MFS1.D1/TX
  N5: Part2.TXO, MFS1.D0/RX
  N6: Part2.GND, MFS1.GND#89

custom parts:
  Multi Function Shield: Das Multi Function Shield kann auf den Arduino Uno aufgesteckt werden und bietet ein paar wichtige Bauteile.
